# Fritzing sketch ssd1306-DFPlayerMini-rpipico (saved by Fritzing 0.9.6b)
breadboards: 1

parts:
  Mod1 = Raspberry Pi Pico
  Part1 = SPI OLED Monochrome 128x64 0.96 inch
  DFRobot_DFPlayer_Mini1 = DFRobot DFPlayer Mini [part_number=DFR0299]
  S1 = Pushbutton [package=THT]
  R1 = Resistor [tolerance=±5% resistance=220 package="0603 [SMD]"]
  SP1 = SPEAKER [package=pcb_mount_speaker]

nets:
  N1: Mod1.pin_3, Mod1.pin_8, Mod1.pin_13, Mod1.pin_18, Mod1.pin_23, Mod1.pin_28, Mod1.pin_33, Mod1.pin_38, Mod1.pin_42, Part1.GND, DFRobot_DFPlayer_Mini1.GND-1, DFRobot_DFPlayer_Mini1.GND-2, S1.leg1
  N2: Mod1.pin_5, Part1.RES
  N3: Mod1.pin_6, Part1.DC
  N4: Mod1.pin_9, Part1.SCK
  N5: Mod1.pin_10, Part1.SDA
  N6: Mod1.pin_19, S1.leg0, R1.Pin_1
  VDD: Mod1.pin_36, Part1.VDD, DFRobot_DFPlayer_Mini1.VCC, R1.Pin_0
  N7: DFRobot_DFPlayer_Mini1.SPK_1, SP1.-
  N8: DFRobot_DFPlayer_Mini1.SPK_2, SP1.+

custom parts:
  Raspberry Pi Pico: Raspberry Pi Pico. Based around the RP2040 microcontroller the Pico is a low cost microcontroller device bringing Raspberry Pi quality, cost, and easy of use to the microcontroller space. Jan 2021, Split part in to two versions: tht (this one) and SMD. This one will drill holes for a .1 in header in pcb to allow plugging in the module as well as providing pads to solder the module to the top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
  SPI OLED Monochrome 128x64 0.96 inch: Unknown 128x64 0.96 inch 128x64 SPI Monochrome OLED display
